# Fritzing sketch motor_driver (saved by Fritzing 0.9.3b)

parts:
  Raspberry_Pi_1 = Raspberry Pi 3 [part_number=RPI-3-V1.2]
  S1 = H-Bridge with L298N
  VCC1 = Battery block 9V
  M1 = DC Motor
  M2 = DC Motor
  M3 = DC Motor
  M4 = DC Motor

nets:
  N1: Raspberry_Pi_1.GPIO2, S1.ENA
  N2: Raspberry_Pi_1.GPIO3, S1.IN1
  N3: Raspberry_Pi_1.GPIO4, S1.IN2
  GND: Raspberry_Pi_1.GND, S1.GND, VCC1.-
  N4: Raspberry_Pi_1.GPIO17, S1.IN3
  N5: Raspberry_Pi_1.GPIO27, S1.IN4
  N6: Raspberry_Pi_1.GPIO22, S1.ENB
  N7: S1.12V, VCC1.+
  N8: S1.M1-01, M1.pin_2, M4.pin_2
  N9: S1.M1-02, M1.pin_1, M4.pin_1
  N10: S1.M2-01, M2.pin_2, M3.pin_2
  N11: S1.M2-02, M2.pin_1, M3.pin_1

custom parts:
  H-Bridge with L298N: h-bridge
